# Fritzing sketch Driver motor Bomba (saved by Fritzing 0.9.3b)
circuit board: 8.46667cm x 5.64444cm

parts:
  Q1 = Basic FET P-Channel [package="TO220 [THT]"]
  Q2 = Basic FET P-Channel [package="TO220 [THT]"]
  Q3 = Basic FET P-Channel [package="TO220 [THT]"]
  Q4 = Basic FET P-Channel [package="TO220 [THT]"]
  R1 = Resistor [tolerance=±5% resistance=220 package=THT]
  J5 = Screw terminal - 2 pins [package=THT]
  D1 = Rectifier Diode [part_number=1N4001 package="300 mil [THT]"]
  J7 = screw terminal, 4 pins

nets:
  N1: Q1.gate, Q2.gate, Q3.gate, Q4.gate, R1.Pin_1
  N2: Q1.drain, Q2.drain, Q3.drain, Q4.drain, D1.anode, J7.pin1
  N3: Q1.source, Q2.source, Q3.source, Q4.source, J5.pin1, J7.pin4
  N4: R1.Pin_0, J5.pin2
  N5: D1.cathode, J7.pin2, J7.pin3
