# Fritzing sketch LCD Bomba (saved by Fritzing 0.9.3b)
circuit board: 8.46667cm x 5.64444cm

parts:
  LCD1 = LCD screen
  R1 = Resistor [tolerance=±5% resistance=220 package=THT]
  J1 = female alternating pin header, 9 pins [form="♀ (female)"]
  J2 = Piezo Speaker

nets:
  N1: LCD1.VSS, LCD1.R/W, LCD1.LED-, R1.Pin_1, J1.pin1, J2.pin1
  N2: LCD1.VDD, LCD1.LED+, J1.pin2
  N3: LCD1.V0, R1.Pin_0
  N4: LCD1.RS, J1.pin3
  N5: LCD1.E, J1.pin4
  N6: LCD1.DB4, J1.pin5
  N7: LCD1.DB5, J1.pin6
  N8: LCD1.DB6, J1.pin7
  N9: LCD1.DB7, J1.pin8
  N10: J1.pin9, J2.pin2
