# Fritzing sketch ModuloRELE2 (saved by Fritzing 0.9.3b)
circuit board: 8.46667cm x 5.64444cm

parts:
  K1 = OMRON PCB Power Relay – G5LE [part_number="G5LE-1\n" package=THT]
  D1 = Rectifier Diode [part_number=1N4001 package="300 mil [THT]"]
  J1 = screw terminal, 3 pins
  J2 = screw terminal, 3 pins
  Q1 = NPN-Transistor [package="TO92 [THT]"]
  R1 = Resistor [tolerance=±5% resistance=220 package=THT]
  F1 = FUSE [package=fuse_5mm]

nets:
  N1: K1.A, J1.pin1
  N2: K1.COIL1, D1.cathode, J2.pin1
  N3: K1.C, F1.1
  N4: K1.COIL2, D1.anode, Q1.E
  N5: K1.B, J1.pin3
  N6: J1.pin2, F1.2
  N7: J2.pin2, R1.Pin_1
  N8: J2.pin3, Q1.C
  N9: Q1.B, R1.Pin_0
