# Fritzing sketch Projeto bomba LCD I2C (saved by Fritzing 0.9.3b)
circuit board: 8.46667cm x 8.04cm

parts:
  Componente1 = Arduino Nano (Rev3.0)
  J1 = shrouded pin header, 10 pins [form="♂ (shrouded male)"]
  R1 = Resistor [tolerance=±5% resistance=220 package=THT]
  U1 = Voltage Regulator - 5V [package="TO220 [THT]"]
  C1 = Electrolytic Capacitor [capacitance=470µF voltage=16V package="100 mil [THT, electrolytic]"]
  D1 = Rectifier Diode [part_number=1N4001 package="300 mil [THT]"]
  C2 = Electrolytic Capacitor [capacitance=470µF voltage=16V package="100 mil [THT, electrolytic]"]
  J4 = Screw terminal - 2 pins [package=THT]
  J3 = screw terminal, 4 pins

nets:
  GND: Componente1.GND, J1.pin10, U1.GND, C1.-, C2.-, J4.pin2, J3.pin1
  N1: Componente1.D2, J1.pin9
  N2: Componente1.D3, J1.pin8
  N3: Componente1.D4, J1.pin7
  N4: Componente1.D5, J1.pin6
  N5: Componente1.D8, J1.pin5
  N6: Componente1.D10, J3.pin4
  N7: Componente1.D11/MOSI, J1.pin4
  N8: Componente1.D12/MISO, J1.pin3
  N9: Componente1.VIN, U1.output_voltage, C2.+
  N10: Componente1.5V, J1.pin2, R1.Pin_1, J3.pin2
  N11: Componente1.A0, R1.Pin_0, J3.pin3
  N12: U1.input_voltage, C1.+, D1.cathode
  N13: D1.anode, J4.pin1
